// Logisim project A.circ as structural Verilog: 1 circuit, main circuit Segment_A
module Segment_A (
  input  [3:0] ABCD,
  output out_2
);

  wire and_1_out, and_2_out, not_1_out, not_2_out, not_3_out, not_4_out, not_5_out, not_6_out, or_1_out;

  not not_1 (not_1_out, ABCD[1]);
  not not_2 (not_2_out, ABCD[2]);
  not not_3 (not_3_out, ABCD[3]);
  not not_4 (not_4_out, ABCD[0]);
  not not_5 (not_5_out, ABCD[1]);
  not not_6 (not_6_out, ABCD[3]);
  and and_1 (and_1_out, ABCD[0], not_1_out, not_2_out, not_3_out);
  and and_2 (and_2_out, not_4_out, not_5_out, ABCD[2], not_6_out);
  or or_1 (or_1_out, and_1_out, and_2_out);
  not not_7 (out_2, or_1_out);
  _7_Segment_Display u_7_segment_display_1 (.a(out_2));  // open: g, f, b, e, d, c, dp
endmodule
