// Logisim project C.circ as structural Verilog: 1 circuit, main circuit Segment_C
module Segment_C (
  input  [3:0] ABCD,
  output out_2
);

  wire and_1_out, not_1_out, not_2_out, not_3_out;

  not not_1 (not_1_out, ABCD[0]);
  not not_2 (not_2_out, ABCD[2]);
  not not_3 (not_3_out, ABCD[3]);
  and and_1 (and_1_out, not_1_out, ABCD[1], not_2_out, not_3_out);
  not not_4 (out_2, and_1_out);
  _7_Segment_Display u_7_segment_display_1 (.c(out_2));  // open: g, f, a, b, e, d, dp
endmodule
