// Logisim project G.circ as structural Verilog: 1 circuit, main circuit Segment_G
module Segment_G (
  input  [3:0] ABCD,
  output out_2
);

  wire and_1_out, and_2_out, and_3_out, not_1_out, not_2_out, not_3_out, not_4_out, not_5_out, not_6_out,
       not_7_out, not_8_out, or_1_out;

  not not_1 (not_1_out, ABCD[0]);
  not not_2 (not_2_out, ABCD[1]);
  not not_3 (not_3_out, ABCD[2]);
  not not_4 (not_4_out, ABCD[3]);
  not not_5 (not_5_out, ABCD[1]);
  not not_6 (not_6_out, ABCD[2]);
  not not_7 (not_7_out, ABCD[3]);
  not not_8 (not_8_out, ABCD[3]);
  and and_1 (and_1_out, not_1_out, not_2_out, not_3_out, not_4_out);
  and and_2 (and_2_out, ABCD[0], not_5_out, not_6_out, not_7_out);
  and and_3 (and_3_out, ABCD[0], ABCD[1], ABCD[2], not_8_out);
  or or_1 (or_1_out, and_1_out, and_2_out, and_3_out);
  not not_9 (out_2, or_1_out);
  _7_Segment_Display u_7_segment_display_1 (.g(out_2));  // open: f, a, b, e, d, c, dp
endmodule
