// Logisim project main.circ as structural Verilog: 1 circuit, main circuit main
module main (
);

  wire clock_1_out, segment_a_1_out_2, segment_b_1_out_2, segment_c_1_out_2, segment_d_1_out_2,
       segment_e_1_out_2, segment_f_1_out_2, segment_g_1_out_2;
  wire [3:0] counter_1_q;

  Counter #(.max('h9), .width(4)) counter_1 (
    .Q(counter_1_q), .clk(clock_1_out));  // open: load, D, count, carry, up, clr
  Clock clock_1 (.out(clock_1_out));
  Segment_A segment_a_1 (.ABCD(counter_1_q), .out_2(segment_a_1_out_2));
  Segment_B segment_b_1 (.ABCD(counter_1_q), .out_2(segment_b_1_out_2));
  Segment_C segment_c_1 (.ABCD(counter_1_q), .out_2(segment_c_1_out_2));
  Segment_D segment_d_1 (.ABCD(counter_1_q), .out_2(segment_d_1_out_2));
  Segment_E segment_e_1 (.ABCD(counter_1_q), .out_2(segment_e_1_out_2));
  Segment_F segment_f_1 (.ABCD(counter_1_q), .out_2(segment_f_1_out_2));
  Segment_G segment_g_1 (.ABCD(counter_1_q), .out_2(segment_g_1_out_2));
  _7_Segment_Display u_7_segment_display_1 (
    .g(segment_g_1_out_2), .f(segment_f_1_out_2), .a(segment_a_1_out_2), .b(segment_b_1_out_2),
    .e(segment_e_1_out_2), .d(segment_d_1_out_2), .c(segment_c_1_out_2));  // open: dp
endmodule
