// Logisim project Alarmanlage1.1.circ as structural Verilog: 1 circuit, main circuit main
module main (
  input  DoorA,
  input  DoorB,
  input  Key
);

  wire and_1_out, not_1_out, not_2_out, or_1_out;

  or or_1 (or_1_out, DoorA, DoorB);
  not not_1 (not_1_out, Key);
  and and_1 (and_1_out, or_1_out, not_1_out);
  not not_2 (not_2_out, and_1_out);
  // RGBLED Alarm: pin names not known; wires that end beside it: and_1_out, not_2_out
endmodule
