// Logisim project Alarmanlage1.2.circ as structural Verilog: 1 circuit, main circuit main
module main (
  input  Door1,
  input  Door2,
  input  Door3,
  input  Key,
  output out_5
);

  wire not_1_out, or_1_out;

  or or_1 (or_1_out, Door1, Door2, Door3);
  not not_1 (not_1_out, Key);
  and and_1 (out_5, or_1_out, not_1_out);
endmodule
