// Logisim project Ampelschaltungen.circ as structural Verilog: 5 circuits, main circuit Ampel1
module Aufgabe1 (
);

  wire ampel1_1_ge, ampel1_1_gr, ampel1_1_r, clock_1_out;
  wire [1:0] counter_1_q;

  Counter #(.max('h3), .width(2)) counter_1 (
    .Q(counter_1_q), .clk(clock_1_out));  // open: load, D, count, carry, up, clr
  Clock clock_1 (.out(clock_1_out));
  LED led_1 (.in(ampel1_1_r));
  Ampel1 ampel1_1 (.A(counter_1_q[1]), .B(counter_1_q[0]), .R(ampel1_1_r), .Ge(ampel1_1_ge), .Gr(ampel1_1_gr));
  LED led_2 (.in(ampel1_1_ge));
  LED led_3 (.in(ampel1_1_gr));

  // Notes on the sheet:
  //   Aufgabe 1
  //   Bearbeiten Sie Ihre Schaltung in der Unterschaltung "Ampel1".
  //   Sollte die Simulation nicht starten, wählen Sie im Menü bitte "Simulieren" -> "weiterschalten aktiv" aus!
endmodule

module Aufgabe2 (
);

  wire ampel2_1_fgr, ampel2_1_fr, ampel2_1_ge, ampel2_1_gr, ampel2_1_r, button_1_out, steuerung_1_a,
       steuerung_1_b, steuerung_1_c;

  Steuerung steuerung_1 (.Request(button_1_out), .A(steuerung_1_a), .B(steuerung_1_b), .C(steuerung_1_c));
  Ampel2 ampel2_1 (
    .A(steuerung_1_a), .B(steuerung_1_b), .C(steuerung_1_c), .R(ampel2_1_r), .Ge(ampel2_1_ge),
    .Gr(ampel2_1_gr), .FR(ampel2_1_fr), .FGr(ampel2_1_fgr));
  LED led_1 (.in(ampel2_1_r));
  LED led_2 (.in(ampel2_1_ge));
  LED led_3 (.in(ampel2_1_gr));
  Button button_1 (.out(button_1_out));
  LED led_4 (.in(ampel2_1_fr));
  LED led_5 (.in(ampel2_1_fgr));

  // Notes on the sheet:
  //   Aufgabe 2
  //   Diese Ampelanlage soll eine Ampel für Fahrzeuge und für Fußgänger schalten.
  //   Bearbeiten Sie Ihre Schaltung in der Unterschaltung "Ampel2".
  //   Drückknopf
  //   Fahrzeuge
  //   Fußgänger
endmodule

module Ampel1 (
  input  A,
  input  B,
  output R,
  output Ge,
  output Gr
);

  wire and_1_out, and_2_out, and_3_out, and_4_out, not_1_out, not_2_out, not_3_out, not_4_out, not_5_out;

  not not_1 (not_1_out, A);
  and and_1 (and_1_out, not_1_out, not_2_out);
  not not_2 (not_2_out, B);
  not not_3 (not_3_out, A);
  and and_2 (and_2_out, not_3_out, B);
  not not_4 (not_4_out, A);
  and and_3 (and_3_out, not_4_out, B);
  and and_4 (and_4_out, A, B);
  and and_5 (Gr, A, not_5_out);
  not not_5 (not_5_out, B);
  or or_1 (R, and_1_out, and_2_out);
  or or_2 (Ge, and_3_out, and_4_out);
endmodule

module Ampel2 (
  input  A,
  input  B,
  input  C,
  output R,
  output Ge,
  output Gr,
  output FR,
  output FGr
);

  wire and_1_out, and_2_out, and_3_out, and_4_out, and_5_out, and_6_out, and_7_out, and_8_out, and_9_out,
       not_1_out, not_2_out, not_3_out, not_4_out, not_5_out, not_6_out, not_7_out, not_8_out, not_9_out,
       not_10_out, not_11_out, not_12_out, not_13_out, not_14_out, or_4_out;

  not not_1 (not_1_out, A);
  and and_1 (and_1_out, not_1_out, B, C);
  not not_2 (not_2_out, B);
  and and_2 (and_2_out, A, not_2_out, not_3_out);
  not not_3 (not_3_out, C);
  not not_4 (not_4_out, A);
  not not_5 (not_5_out, B);
  and and_3 (and_3_out, not_4_out, not_5_out, not_6_out);
  not not_6 (not_6_out, C);
  and and_4 (and_4_out, A, B, C);
  not not_7 (not_7_out, A);
  not not_8 (not_8_out, B);
  and and_5 (and_5_out, not_7_out, not_8_out, C);
  and and_6 (and_6_out, A, B, not_9_out);
  not not_9 (not_9_out, C);
  not not_10 (not_10_out, A);
  not not_11 (not_11_out, B);
  and and_7 (and_7_out, not_10_out, not_11_out, not_12_out);
  not not_12 (not_12_out, C);
  not not_13 (not_13_out, A);
  not not_14 (not_14_out, B);
  and and_8 (and_8_out, not_13_out, not_14_out, C);
  and and_9 (and_9_out, A, B, C);
  or or_1 (FGr, and_1_out, and_2_out);
  or or_2 (Gr, and_3_out, and_4_out);
  or or_3 (Ge, and_5_out, and_6_out);
  or or_4 (or_4_out, and_7_out, and_9_out);
  not not_15 (R, or_4_out);
  not not_16 (FR, FGr);
endmodule

module Steuerung (
  input  Request,
  output A,
  output B,
  output C
);

  wire clock_1_out;

  Clock clock_1 (.out(clock_1_out));
  Counter #(.max('h7), .ongoal("stay"), .width(3)) counter_1 (
    .Q({A, B, C}), .clk(clock_1_out), .clr(Request));  // open: load, D, count, carry, up

  // Notes on the sheet:
  //   Sie dient der Steuerung des Zählwerks
  //   Sie brauchen diese Art von Schaltung noch nicht zu verstehen.
endmodule
