// Logisim project main.circ as structural Verilog: 1 circuit, main circuit main
module main (
  input  \Schlüssel ,
  input  \Tür ,
  input  Freundin_ruft_an,
  input  Fenster,
  input  Klausur,
  input  Bewegungsalarm,
  input  Dienstag,
  input  NAND,
  input  Aufgabe_4,
  input  in_10,
  input  in_11,
  input  in_12,
  input  in_13,
  input  in_14,
  input  in_15,
  input  in_16,
  input  in_17,
  input  XOR,
  input  in_19,
  input  NOR,
  input  in_21,
  input  XNOR,
  input  in_23,
  output LED,
  output Alarm,
  output Ausgehen,
  output out_27,
  output out_28,
  output out_29,
  output out_30,
  output out_31,
  output out_32,
  output out_33,
  output out_34,
  output out_35
);

  wire nand_2_out, or_1_out;

  not not_1 (LED, \Schlüssel );
  or or_1 (or_1_out, \Tür , Fenster, Bewegungsalarm);
  nand nand_1 (out_28, NAND, in_14);
  xor xor_1 (out_33, XOR, in_19);
  nor nor_1 (out_34, NOR, in_21);
  xnor xnor_1 (out_35, XNOR, in_23);
  and and_1 (Alarm, LED, or_1_out);
  not not_2 (out_27, Aufgabe_4);
  ExactlyOne xor_2 (.out(Ausgehen), .in0(Freundin_ruft_an), .in1(Klausur), .in2(Dienstag));
  and and_2 (out_29, in_10, in_15);
  or or_2 (out_30, in_11, in_16);
  nand nand_2 (nand_2_out, in_12, in_17);
  nand nand_3 (out_31, nand_2_out, nand_2_out);
  nand nand_4 (out_32, in_13, in_13);

  // Notes on the sheet:
  //   Aufgabe 1
  //   Aufgabe 2
  //   Aufgabe 3
endmodule
