// Logisim project RS_Flipflop.circ as structural Verilog: 1 circuit, main circuit main
module main (
  input  S,
  input  R,
  output QQ,
  output Q
);

  wire or_1_out, or_2_out;

  or or_1 (or_1_out, S, Q);
  not not_1 (QQ, or_1_out);
  or or_2 (or_2_out, QQ, R);
  not not_2 (Q, or_2_out);

  // Notes on the sheet:
  //   RS_Flipflop
endmodule
