// Logisim project main.circ as structural Verilog: 1 circuit, main circuit main
module main (
  input  Kommutativgesetz,
  input  Assoziativgesetz,
  input  a,
  input  a_2,
  input  b,
  input  b_2,
  input  b_3,
  input  c,
  input  a_3,
  input  c_2,
  input  b_4,
  input  a_4,
  input  a_5,
  input  a_6,
  input  b_5,
  input  b_6,
  input  c_3,
  input  c_4,
  input  a_7,
  input  Extremalgesetz,
  input  a_8,
  input  a_9,
  input  _1,
  input  _0,
  input  a_10,
  input  b_7,
  input  a_11,
  input  a_12,
  input  _0_2,
  input  b_8,
  input  \Dualitätsgesetz ,
  input  a_13,
  input  a_14,
  input  _1_2,
  input  b_9,
  input  _0_3,
  input  a_15,
  output out_38,
  output out_39,
  output out_40,
  output out_41,
  output out_42,
  output out_43,
  output out_44,
  output out_45,
  output out_46,
  output out_47,
  output out_48,
  output out_49,
  output out_50,
  output out_51,
  output out_52,
  output out_53,
  output out_54,
  output out_55,
  output out_56,
  output out_57,
  output out_58,
  output out_59
);

  wire and_5_out, and_6_out, and_10_out, and_13_out, and_14_out, and_15_out, and_17_out, not_1_out,
       not_3_out, not_5_out, not_6_out;

  and and_1 (out_38, Kommutativgesetz, b);
  and and_2 (out_43, b_4, a_5);
  and and_3 (out_47, a_7, _1);
  not not_1 (not_1_out, a_14);
  and and_4 (out_56, a_14, not_1_out);
  and and_5 (and_5_out, Assoziativgesetz, b_2);
  and and_6 (and_6_out, b_5, c_3);
  and and_7 (out_48, Extremalgesetz, _0);
  not not_2 (out_54, \Dualitätsgesetz );
  and and_8 (out_40, and_5_out, c);
  and and_9 (out_44, a_4, and_6_out);
  not not_3 (not_3_out, a_8);
  and and_10 (and_10_out, a_13, b_9);
  and and_11 (out_39, a, a);
  not not_4 (out_46, not_3_out);
  and and_12 (out_55, a_13, and_10_out);
  and and_13 (and_13_out, a_9, b_7);
  not not_5 (not_5_out, a_11);
  not not_6 (not_6_out, b_8);
  and and_14 (and_14_out, b_3, c_2);
  and and_15 (and_15_out, a_6, b_6);
  not not_7 (out_49, and_13_out);
  or or_1 (out_53, not_5_out, not_6_out);
  and and_16 (out_41, a_2, and_14_out);
  and and_17 (and_17_out, a_6, c_4);
  or or_2 (out_45, and_15_out, and_17_out);

  assign out_42 = a_3;
  assign out_50 = a_10;
  assign out_51 = a_12;
  assign out_52 = _0_2;
  assign out_57 = _1_2;
  assign out_58 = _0_3;
  assign out_59 = a_15;

  // Notes on the sheet:
  //   a
  //   Neutralitätsgesetz
  //   Komplementärgesetz
  //   a
  //   a
  //   0
  //   Doppelnegationsgesetz
  //   Absorptionsgesetz
  //   Idempotenzgesetz
  //   Distributivgesetz
  //   De Morgansche Gesetz
endmodule
