// Logisim project main.circ as structural Verilog: 1 circuit, main circuit Halbaddierer
module Halbaddierer (
  input  A,
  input  B,
  output R,
  output C
);

  xor xor_1 (R, A, B);
  and and_1 (C, A, B);
endmodule
