// Logisim project Rechenwerk.circ as structural Verilog: 1 circuit, main circuit main
module main (
  input  [7:0] A,
  input  [7:0] B,
  input  C,
  output C_out,
  output [7:0] R
);

  wire volladdierer_1_cout, volladdierer_2_cout, volladdierer_3_cout, volladdierer_4_cout,
       volladdierer_5_cout, volladdierer_6_cout, volladdierer_7_cout;

  Volladdierer volladdierer_1 (.A(A[0]), .B(B[0]), .C(C), .Cout(volladdierer_1_cout), .R(R[0]));
  Volladdierer volladdierer_2 (.A(A[1]), .B(B[1]), .C(volladdierer_1_cout), .Cout(volladdierer_2_cout), .R(R[1]));
  Volladdierer volladdierer_3 (.A(A[2]), .B(B[2]), .C(volladdierer_2_cout), .Cout(volladdierer_3_cout), .R(R[2]));
  Volladdierer volladdierer_4 (.A(A[3]), .B(B[3]), .C(volladdierer_3_cout), .Cout(volladdierer_4_cout), .R(R[3]));
  Volladdierer volladdierer_5 (.A(A[4]), .B(B[4]), .C(volladdierer_4_cout), .Cout(volladdierer_5_cout), .R(R[4]));
  Volladdierer volladdierer_6 (.A(A[5]), .B(B[5]), .C(volladdierer_5_cout), .Cout(volladdierer_6_cout), .R(R[5]));
  Volladdierer volladdierer_7 (.A(A[6]), .B(B[6]), .C(volladdierer_6_cout), .Cout(volladdierer_7_cout), .R(R[6]));
  Volladdierer volladdierer_8 (.A(A[7]), .B(B[7]), .C(volladdierer_7_cout), .Cout(C_out), .R(R[7]));
endmodule
