// Logisim project Volladdierer.circ as structural Verilog: 1 circuit, main circuit Volladdierer
module Volladdierer (
  input  A,
  input  B,
  input  C,
  output Cout,
  output R
);

  wire halbaddierer_1_p3, halbaddierer_1_p4, halbaddierer_2_p2;

  // Halbaddierer halbaddierer_1: pin names not known; wires that end beside it: A, B, halbaddierer_1_p3, halbaddierer_1_p4, halbaddierer_1_p3, C
  or or_1 (Cout, halbaddierer_1_p4, halbaddierer_2_p2);
  // Halbaddierer halbaddierer_2: pin names not known; wires that end beside it: R, halbaddierer_2_p2
endmodule
